# Fritzing sketch 2Tree_Brain (saved by Fritzing 0.9.10b)
breadboards: 1

parts:
  Mod1 = Raspberry Pi 4B
  S1 = SWITCH-DPDT [package=mss22]
  External_TRS_Jack = Audio Jack (TRS) 3.5mm [package="PG203J [THT]"]
  Power_plug1 = Power plug
  Pi_TRS_Out = Audio Jack (TRS) 3.5mm [package="PG203J [THT]"]
  SP1 = SPEAKER [package=pcb_mount_speaker]
  Part1 = Mono 2.5W Class D Audio Amplifier - PAM8302
  BUTTON2 = Waterproof Pushbutton (blue)
  BUTTON3 = Waterproof Pushbutton (blue)
  BUTTON4 = Waterproof Pushbutton (blue)
  BUTTON5 = Waterproof Pushbutton (blue)

nets:
  VCC: Mod1.5V, Power_plug1.VCC, Part1.VCC
  GND: Mod1.GND, Power_plug1.GND, Part1.GND, BUTTON2.no_name_yet, BUTTON3.no_name_yet, BUTTON4.no_name_yet, BUTTON5.no_name_yet
  N1: S1.1, Part1.AIN+
  N2: S1.2, Pi_TRS_Out.Ring
  N3: S1.3, External_TRS_Jack.Ring
  N4: S1.5, Pi_TRS_Out.Tip
  N5: S1.6, External_TRS_Jack.Tip
  N6: External_TRS_Jack.Sleeve, Pi_TRS_Out.Sleeve, Part1.AIN-
  N7: SP1.+, Part1.VO+
  N8: SP1.-, Part1.VO-

custom parts:
  Mono 2.5W Class D Audio Amplifier - PAM8302: A super small but powerful mono amplifier able to deliver up to 2.5 Watts into 4-8 ohm impedance speakers. Inside the miniature chip is a class D controller, able to run from 2.0V-5.5VDC. Since the amp is a class D, its very efficient (over 90% efficient when driving an 8Ω speaker at over half a Watt) - making it perfect for portable and battery-powered projects.
  Waterproof Pushbutton (blue): Waterproof Illuminated Pushbutton (blue)
